# Fritzing sketch WindowLight (saved by Fritzing 0.9.1b)

parts:
  Part1 = Arduino Uno (Rev3)
  NEOPIXEL1 = Neopixel Strip -- Black (30/m)
  RF1 = nRF8001 Bluetooth LE Breakout

nets:
  N1: Part1.D8, NEOPIXEL1.Din
  N2: Part1.D9_PWM, RF1.RST, RF1.3Vo
  N3: Part1.D10_PWM/SS, RF1.REQ
  N4: Part1.D11_PWM/MOSI, RF1.MOSI
  N5: Part1.D12/MISO, RF1.MISO
  N6: Part1.D13/SCK, RF1.SCK
  N7: Part1.D2, RF1.RDY, RF1.ACT
  5V: Part1.5V, NEOPIXEL1.+5V, RF1.VIN
  GND: Part1.GND, NEOPIXEL1.GND, RF1.GND

custom parts:
  Neopixel Strip -- Black (30/m): These NeoPixel strips have 30 digitally-addressable pixel LEDs per meter and are very affordable and are only 12.5 mm wide, 10 mm if you remove the strip from the casing.
  nRF8001 Bluetooth LE Breakout: nRF8001 Breakout Board
